# Fritzing sketch PCB (saved by Fritzing 0.9.6b)
circuit board: 10.2319cm x 5.42488cm
breadboards: 1

parts:
  S1 = Pushbutton [package="[THT]"]
  S2 = Pushbutton [package="[THT]"]
  J3 = female pin header, 1 pin [form="♀ (female)"]
  J4 = female pin header, 1 pin [form="♀ (female)"]
  Part1 = Arduino Mega ADK (Rev3)
  J1 = female pin header, 5 pins [form="♀ (female)"]
  J5 = Screw terminal - 2 pins [package=THT]

nets (from the pcb view):
  N1: S1.Pin_1, S1.Pin_2, S2.Pin_1, S2.Pin_2, J3.pin1, Part1.GND, J1.pin2, J5.pin1
  N2: S1.Pin_3, S1.Pin_4, Part1.D3_PWM
  N3: S2.Pin_3, S2.Pin_4, Part1.D2_PWM
  N4: J4.pin1, Part1.D9_PWM
  N5: Part1.D12_PWM, J1.pin3
  N6: Part1.D11_PWM, J1.pin5
  N7: Part1.D10_PWM, J1.pin4
  N8: Part1.5V, J1.pin1
  N9: Part1.VIN, J5.pin2

notes:
  Asteroids Game
  Henry Quillin
  3-26-2021
