# Fritzing sketch breadboard (saved by Fritzing 0.9.6b)
circuit board: 10.2319cm x 5.42488cm
breadboards: 1

parts:
  S1 = Pushbutton [package="[THT]"]
  S2 = Pushbutton [package="[THT]"]
  Part1 = Arduino Mega ADK (Rev3)
  8x8_LED_Modul_mit_MAX1 = 8x8 LED Modul mit MAX7219 [package=THT]
  J6 = Piezo Speaker
  VCC1 = Battery block 9V

nets (from the breadboard view):
  N1: S1.Pin_1, S1.Pin_2, Part1.D3_PWM
  N2: S1.Pin_3, S1.Pin_4, S2.Pin_3, S2.Pin_4, Part1.GND, 8x8_LED_Modul_mit_MAX1.GND_Eingang, J6.pin1, VCC1.-
  N3: S2.Pin_1, S2.Pin_2, Part1.D2_PWM
  N4: Part1.D12_PWM, 8x8_LED_Modul_mit_MAX1.DIN_Eingang
  N5: Part1.D11_PWM, 8x8_LED_Modul_mit_MAX1.CLK_Eingang
  N6: Part1.D10_PWM, 8x8_LED_Modul_mit_MAX1.CS_Eingang
  N7: Part1.D9_PWM, J6.pin2
  N8: Part1.5V, 8x8_LED_Modul_mit_MAX1.VCC_Eingang
  N9: Part1.VIN, VCC1.+

notes:
  Asteroids Game
  Henry Quillin
  3-26-2021
